// Logisim project tp_4_1.circ as structural Verilog: 6 circuits, main circuit basculeRS
module main (
  input  S,
  input  R,
  output Q,
  output nQ
);

  nand nand_1 (Q, S, nQ);
  nand nand_2 (nQ, Q, R);
endmodule

module add_un (
  input  C,
  input  A,
  input  B,
  output Somme,
  output Retenue
);

  wire and_1_out, and_2_out, xor_1_out;

  xor xor_1 (xor_1_out, A, B);
  and and_1 (and_1_out, A, B);
  xor xor_2 (Somme, C, xor_1_out);
  buf and_2 (and_2_out, xor_1_out);  // AND_Gate
  or or_1 (Retenue, and_2_out, and_1_out);
endmodule

module basculeRS (
  input  S,
  input  R,
  output Q,
  output nQ
);

  nand nand_1 (Q, S, nQ);
  nand nand_2 (nQ, Q, R);
endmodule

module VerrouD (
  input  D,
  input  W,
  output Q,
  output nQ
);

  wire nand_1_out, nand_2_out;

  nand nand_1 (nand_1_out, D, W);
  nand nand_2 (nand_2_out, nand_1_out, W);
  nand nand_3 (Q, nand_1_out, nQ);
  nand nand_4 (nQ, Q, nand_2_out);
endmodule

module basculeD (
  input  in_1,
  input  in_2,
  output Q,
  output nQ
);

  wire not_1_out, verroud_1_q;

  not not_1 (not_1_out, in_2);
  VerrouD verroud_1 (.D(in_1), .W(not_1_out), .Q(verroud_1_q));  // open: nQ
  VerrouD verroud_2 (.D(verroud_1_q), .W(in_2), .Q(Q), .nQ(nQ));
endmodule

module compteur10 (
);

  wire undriven, undriven_2, undriven_3, undriven_4, undriven_5, undriven_6;

  basculeD basculed_1 (.in_1(undriven_5), .in_2(undriven_6));  // open: Q, nQ
  basculeD basculed_2 (.in_1(undriven_4), .in_2(undriven_6));  // open: Q, nQ
  basculeD basculed_3 (.in_1(undriven_3), .in_2(undriven_6));  // open: Q, nQ
  basculeD basculed_4 (.in_1(undriven_2), .in_2(undriven_6));  // open: Q, nQ
  basculeD basculed_5 (.in_1(undriven), .in_2(undriven_6));  // open: Q, nQ
endmodule
